# Fritzing sketch seguidor de linea 1.0 (saved by Fritzing 0.9.3b)
circuit board: 6.431cm x 4.95767cm

parts:
  ARDUINO_NANO = Arduino Nano (Rev3.0)
  TB6612FNG = Motor Driver 1A Dual TB6612FNG
  R1 = Resistor [tolerance=±5% resistance=220 package=THT]
  LED1 = LED - 5mm [color="Red (633nm)" package="5 mm [THT]"]
  M1 = DC Motor
  M2 = DC Motor
  C1 = Tantalum Capacitor [capacitance=1μF package="100 mil [THT, tantalum]"]
  C2 = Tantalum Capacitor [capacitance=1μF package="100 mil [THT, tantalum]"]
  2-1 = DC Motor
  6-5 = DC Motor
  8-7 = DC Motor
  R2 = Resistor [tolerance=±5% resistance=220 package=THT]
  D11-5V = DC Motor
  GND = DC Motor
  C3 = Tantalum Capacitor [capacitance=1μF package="100 mil [THT, tantalum]"]
  4-3 = DC Motor

nets:
  GND: ARDUINO_NANO.GND, TB6612FNG.GND, R2.Pin_1, GND.pin_2, C3.+
  N1: ARDUINO_NANO.D3, TB6612FNG.PWMB
  N2: ARDUINO_NANO.D4, TB6612FNG.BIN2
  N3: ARDUINO_NANO.D5, TB6612FNG.BIN1
  N4: ARDUINO_NANO.D6, TB6612FNG.STBY
  N5: ARDUINO_NANO.D7, TB6612FNG.AIN1
  N6: ARDUINO_NANO.D8, TB6612FNG.AIN2
  N7: ARDUINO_NANO.D9, TB6612FNG.PWMA
  N8: ARDUINO_NANO.D11/MOSI, D11-5V.pin_2
  N9: ARDUINO_NANO.D12/MISO, C1.+, R2.Pin_0
  N10: ARDUINO_NANO.VIN, TB6612FNG.VM, C2.-
  5V: ARDUINO_NANO.5V, TB6612FNG.VCC, C1.-, D11-5V.pin_1
  N11: ARDUINO_NANO.A7, 8-7.pin_1
  N12: ARDUINO_NANO.A6, 8-7.pin_2
  N13: ARDUINO_NANO.A5, 6-5.pin_1
  N14: ARDUINO_NANO.A4, 6-5.pin_2
  N15: ARDUINO_NANO.A3, 4-3.pin_1
  N16: ARDUINO_NANO.A2, 4-3.pin_2
  N17: ARDUINO_NANO.A1, 2-1.pin_1
  N18: ARDUINO_NANO.A0, 2-1.pin_2
  N19: ARDUINO_NANO.D13/SCK, LED1.cathode
  N20: TB6612FNG.B01, M2.pin_1
  N21: TB6612FNG.B02, M2.pin_2
  N22: TB6612FNG.A02, M1.pin_2
  N23: TB6612FNG.A01, M1.pin_1
  N24: R1.Pin_0, LED1.anode
  N25: C2.+, C3.-

notes:
  SEGUIDOR 1.0
  EL ING ANDRES
